# Fritzing sketch FunctionProofPCB (saved by Fritzing 0.9.3b)
circuit board: 3.89059cm x 2.97807cm
breadboards: 1

parts:
  6DOF1 = female pin header, 8 pins [form="♀ (female)"]
  Teensy_3_2 = female pin header, 14 pins [form="♀ (female)"]
  Teensy_3_2_2 = female pin header, 14 pins [form="♀ (female)"]
  5V_GND = female pin header, 2 pins [form="♀ (female)"]
  SWITCH = female pin header, 2 pins [form="♀ (female)"]
  OLED1&4 = female pin header, 4 pins [form="♀ (female)"]
  OLED1&5 = female pin header, 4 pins [form="♀ (female)"]
  SPEAKER1 = female pin header, 2 pins [form="♀ (female)"]
  BUTTON = female pin header, 2 pins [form="♀ (female)"]
  10k1 = Resistor [tolerance=±5% resistance=10 package=THT]

nets:
  N1: 6DOF1.pin5, Teensy_3_2.pin6, OLED1&4.pin4, OLED1&5.pin4
  N2: 6DOF1.pin6, Teensy_3_2.pin7, OLED1&4.pin3, OLED1&5.pin3
  N3: 6DOF1.pin7, Teensy_3_2_2.pin14, 5V_GND.pin1, OLED1&4.pin1, OLED1&5.pin1, 10k1.Pin_1
  N4: 6DOF1.pin8, Teensy_3_2.pin14, SWITCH.pin1, OLED1&4.pin2, OLED1&5.pin2, SPEAKER1.pin1, BUTTON.pin2
  N5: Teensy_3_2.pin5, SPEAKER1.pin2
  N6: Teensy_3_2_2.pin11, BUTTON.pin1, 10k1.Pin_0
  N7: 5V_GND.pin2, SWITCH.pin2

notes:
  Sidney McAdams
  Hackberry Lab
  2/2018
